// Logisim project circuito.circ as structural Verilog: 1 circuit, main circuit main
module main (
  input  Op5,
  input  Op4,
  input  Op3,
  input  Op2,
  input  Op1,
  input  Op0,
  output AluSRC,
  output branch,
  output R_format,
  output lw,
  output sw,
  output beq,
  output jump
);

  wire not_1_out, not_2_out, not_3_out, not_4_out, not_5_out, not_6_out, not_7_out, not_8_out, not_9_out,
       not_10_out, not_11_out, not_12_out, not_13_out, not_14_out, not_15_out, not_16_out, not_17_out,
       not_18_out, not_19_out, not_20_out, not_21_out;

  not not_1 (not_1_out, Op3);
  not not_2 (not_2_out, Op4);
  not not_3 (not_3_out, Op5);
  and and_1 (R_format, not_3_out, not_2_out, not_1_out, not_6_out, not_5_out, not_4_out);
  not not_4 (not_4_out, Op0);
  not not_5 (not_5_out, Op1);
  not not_6 (not_6_out, Op2);
  not not_7 (not_7_out, Op4);
  not not_8 (not_8_out, Op3);
  not not_9 (not_9_out, Op4);
  not not_10 (not_10_out, Op2);
  and and_2 (lw, Op5, not_7_out, not_8_out, not_10_out, Op1, Op0);
  not not_11 (not_11_out, Op5);
  not not_12 (not_12_out, Op2);
  and and_3 (sw, Op5, not_9_out, Op3, not_12_out, Op1, Op0);
  not not_13 (not_13_out, Op0);
  not not_14 (not_14_out, Op3);
  not not_15 (not_15_out, Op4);
  not not_16 (not_16_out, Op1);
  and and_4 (beq, not_11_out, not_15_out, not_14_out, Op2, not_16_out, not_13_out);
  not not_17 (not_17_out, Op4);
  not not_18 (not_18_out, Op5);
  not not_19 (not_19_out, Op0);
  not not_20 (not_20_out, Op2);
  not not_21 (not_21_out, Op3);
  and and_5 (jump, not_18_out, not_17_out, not_21_out, not_20_out, Op1, not_19_out);
  or or_1 (AluSRC, lw, sw);

  assign branch = beq;
endmodule
